# Fritzing sketch Module (saved by Fritzing 0.9.3b)
breadboards: 1

parts:
  U2 = NodeMCU V1.0
  T1 = LM35 Temperature Sensor [package="TO92 [THT]"]

nets:
  N1: U2.3V3, T1.+Vs
  GND: U2.GND, T1.GND
  N2: U2.A0, T1.Vout

custom parts:
  NodeMCU V1.0: ESP8266 based NodeMCU V1.0
